# Fritzing sketch Projet Robotique Full (saved by Fritzing 0.9.3b)
breadboards: 1

parts:
  Composant1 = Arduino Nano (Rev3.0)
  S1 = H-Bridge with L298N
  M1 = DC Motor
  M2 = DC Motor
  VCC1 = Battery block 9V
  D2F1 = D2F-FL Omron Snap Action Limit Switch with Level
  D2F2 = D2F-FL Omron Snap Action Limit Switch with Level
  R1 = PHOTOCELL [package=photocell]
  R2 = PHOTOCELL [package=photocell]
  R3 = PHOTOCELL [package=photocell]
  BT1 = Bluetooth HC-06u [package=THT]
  R4 = Resistor [tolerance=±5% resistance=470 package="1206 [SMD]"]
  R5 = Resistor [tolerance=±5% resistance=470 package="1206 [SMD]"]
  R6 = Resistor [tolerance=±5% resistance=470 package="1206 [SMD]"]
  R7 = Resistor [tolerance=±5% resistance=1k package="1206 [SMD]"]
  R8 = Resistor [tolerance=±5% resistance=680 package="0805 [SMD]"]
  hc-sr1 = hc-sr04
  J2 = Basic Servo

nets:
  N1: Composant1.D1/TX, R7.Pin_1, R8.Pin_1
  N2: Composant1.D0/RX, BT1.TXD
  GND: Composant1.GND, S1.GND, VCC1.-, D2F1.NC, D2F2.NC, BT1.GND, R4.Pin_1, R5.Pin_1, R6.Pin_1, R7.Pin_0, hc-sr1.GND, J2.gnd
  N3: Composant1.D2, D2F2.NO
  N4: Composant1.D3, S1.ENB
  N5: Composant1.D4, S1.IN4
  N6: Composant1.D5, S1.IN3
  N7: Composant1.D6, S1.IN2
  N8: Composant1.D7, S1.IN1
  N9: Composant1.D8, S1.ENA
  N10: Composant1.D9, D2F1.NO
  N11: Composant1.D10, J2.pulse
  N12: Composant1.D11/MOSI, hc-sr1.Trig
  N13: Composant1.D12/MISO, hc-sr1.Echo
  VIN: Composant1.VIN, S1.12V, VCC1.+
  VCC: Composant1.5V, R1.P$1, R2.P$1, R3.P$1, BT1.VCC, hc-sr1.VCC, J2.vcc
  N14: Composant1.A2, R1.P$2, R4.Pin_0
  N15: Composant1.A1, R2.P$2, R6.Pin_0
  N16: Composant1.A0, R3.P$2, R5.Pin_0
  N17: S1.M1-01, M1.pin_2
  N18: S1.M1-02, M1.pin_1
  N19: S1.M2-01, M2.pin_2
  N20: S1.M2-02, M2.pin_1
  N21: BT1.RXD, R8.Pin_0

notes:
  ne JAMAIS brancher la pile en même temps que l'USB
  En cas de MAJ arduino, Débrancher le module

custom parts:
  H-Bridge with L298N: h-bridge
  D2F-FL Omron Snap Action Limit Switch with Level: Snap action switch with stainless steel lever.
  Bluetooth HC-06u: Bluetooth HC-06 - face up, pins down 16.5mm x 37.5mm PCB

// code stored in the sketch: CodeFull.ino
h
